# Fritzing sketch esp32-tresor (saved by Fritzing 0.9.3b)
breadboards: 1

parts:
  U2 = ESP32S-HiLetgo [part_number=ESP32S-HiLetgo]
  J1 = Piezo Speaker
  Q1 = NPN-Transistor [package="TO92 [THT]"]
  R1 = Resistor [tolerance=±5% resistance=220 package="0603 [SMD]"]
  M1 = DC Motor
  3x_AA_Batteries = 4 x AAA Battery Mount
  KEYPAD1 = Membrane Matrix Keypad
  R2 = Resistor [tolerance=±5% resistance=100k package="0603 [SMD]"]
  D1 = Diode [package=diode-1n4148]
  PCB2 = RTC_DS1302_module

nets:
  N1: U2.3.3, R2.Pin_0, PCB2.VCC
  N2: U2.GPIO39, KEYPAD1.5, R2.Pin_1
  N3: U2.GPIO26, PCB2.CLK
  N4: U2.GPIO27, PCB2.DAT
  N5: U2.GPIO14, PCB2.RST
  N6: U2.GPIO17, J1.pin1
  N7: U2.GPIO23, R1.Pin_0
  GND: J1.pin2, Q1.E, 3x_AA_Batteries.-, KEYPAD1.4, PCB2.GND
  N8: Q1.B, R1.Pin_1
  N9: Q1.C, M1.pin_2, D1.C
  N10: M1.pin_1, 3x_AA_Batteries.+, D1.A

custom parts:
  ESP32S-HiLetgo: HiLetgo ESP-WROOM-32 ESP32 ESP-32S Development Board 2.4GHz Dual-Mode WiFi + Bluetooth Dual Cores Microcontroller The ESP32 integrated with Antenna switches, RF Balun, power amplifiers, low-noise amplifiers, filters, and management modules, and the entire solution occupies the least area of PCB. 2.4 GHz Wi-Fi plus Bluetooth dual-mode chip, with TSMC Ultra-low power consumption 40nm technology,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
  Membrane Matrix Keypad: Membrane Matrix 3x4 Keypad
  RTC_DS1302_module: Arduino module DS1302 SPI Real Time Clock
